# Fritzing sketch circuit hand sign language functional (saved by Fritzing 0.9.3b)
breadboards: 1

parts:
  R1 = Basic Flex Resistor
  R2 = Basic Flex Resistor
  R3 = Basic Flex Resistor
  R4 = Basic Flex Resistor
  R5 = Basic Flex Resistor
  Part1 = Bluetooth HC-05 Macho
  Part2 = Arduino Nano (Rev3.0) (ICSP)
  R6 = Resistor [tolerance=±5% resistance=220 package="0805 [SMD]"]
  R7 = Resistor [tolerance=±5% resistance=220 package="0805 [SMD]"]
  R8 = Resistor [tolerance=±5% resistance=220 package="0805 [SMD]"]
  R9 = Resistor [tolerance=±5% resistance=220 package="0805 [SMD]"]
  R10 = Resistor [tolerance=±5% resistance=220 package="0805 [SMD]"]

nets:
  N1: R1.Pin_2, R2.Pin_2, R3.Pin_2, R4.Pin_2, R5.Pin_2, Part2.5V
  N2: R1.pin_1, Part2.A0, R6.Pin_1
  N3: R2.pin_1, Part2.A1, R7.Pin_1
  N4: R3.pin_1, Part2.A2, R8.Pin_1
  N5: R4.pin_1, Part2.A3, R9.Pin_1
  N6: R5.pin_1, Part2.A4, R10.Pin_1
  N7: Part1.TXD, Part2.D10
  N8: Part1.RXD, Part2.D9
  VCC: Part1.VCC, Part2.3V3
  GND: Part1.GND, Part2.GND, R6.Pin_0, R7.Pin_0, R8.Pin_0, R9.Pin_0, R10.Pin_0
